# Fritzing sketch alyrp-leonardo-i2c (saved by Fritzing 0.9.3b)
breadboards: 1

parts:
  Componente1 = Arduino Leonardo (Rev3b)
  Componente2 = MicroSD Card Module
  S1 = Pushbutton [package="[THT]"]
  S2 = Pushbutton [package="[THT]"]
  R1 = Resistor [tolerance=±5% resistance=10k package="0603 [SMD]"]
  R2 = Resistor [tolerance=±5% resistance=10k package="0603 [SMD]"]
  U2 = LCD-16X2 [package=lcd-16x2]

nets:
  N1: Componente1.D2/SDA, U2.VDD
  N2: Componente1.D3_PWM/SCL, U2.VSS
  N3: Componente1.D4/A6, S1.Pin_1, S1.Pin_2, R2.Pin_0
  N4: Componente1.5V, S1.Pin_3, S1.Pin_4, S2.Pin_3, S2.Pin_4, R1.Pin_1, R2.Pin_1, U2.VO
  GND: Componente1.GND, Componente2.GND, U2.RS
  N5: Componente1.D9_PWM/A9, S2.Pin_1, S2.Pin_2, R1.Pin_0
  N6: Componente1.D10_PWM/A10, Componente2.CS

notes:
  i2c module is not a native frtizing component, so refer to this pinout
  green = SCL
  blue = SDA
  red = VCC
  black = GND
