# Fritzing sketch alyrp-uno-noi2c (saved by Fritzing 0.9.3b)
breadboards: 1

parts:
  Componente1 = Arduino Uno (Rev3)
  LCD1 = LCD screen
  Componente2 = MicroSD Card Module
  R1 = Rotary Potentiometer (Small) [maximum_resistance=10kΩ package=THT]
  R2 = Resistor [tolerance=±5% resistance=220 package="0603 [SMD]"]

nets:
  N1: Componente1.D8, LCD1.RS
  N2: Componente1.D10_PWM/SS, Componente2.CS
  N3: Componente1.D2, LCD1.DB7
  N4: Componente1.D3_PWM, LCD1.DB6
  N5: Componente1.D5_PWM, LCD1.DB4
  N6: Componente1.D6_PWM, LCD1.DB5
  N7: Componente1.D7, LCD1.E
  5V: Componente1.5V, LCD1.VDD, R1.leg2, R2.Pin_1
  GND: Componente1.GND, LCD1.VSS, LCD1.R/W, LCD1.LED-, R1.leg1
  N8: LCD1.V0, R1.wiper
  N9: LCD1.LED+, R2.Pin_0
