# Fritzing sketch alyrp-uno-without-i2c (saved by Fritzing 0.9.3b)
breadboards: 1

parts:
  Componente1 = Arduino Uno (Rev3)
  LCD1 = LCD screen
  Componente2 = MicroSD Card Module
  R1 = Rotary Potentiometer (Small) [maximum_resistance=10kΩ package=THT]
  R2 = Resistor [tolerance=±5% resistance=220 package="0603 [SMD]"]
  S1 = Pushbutton [package="[SMD]"]
  S2 = Pushbutton [package="[SMD]"]
  R3 = Resistor [tolerance=±5% resistance=10k package="2010 [SMD]"]
  R4 = Resistor [tolerance=±5% resistance=10k package="2010 [SMD]"]

nets:
  N1: Componente1.D8, LCD1.RS
  N2: Componente1.D9_PWM, S1.Pin_1, S1.Pin_2, R3.Pin_0
  N3: Componente1.D10_PWM/SS, Componente2.CS
  N4: Componente1.D2, S2.Pin_1, S2.Pin_2, R4.Pin_0
  N5: Componente1.D3_PWM, LCD1.DB7
  N6: Componente1.D4, LCD1.DB6
  N7: Componente1.D5_PWM, LCD1.DB5
  N8: Componente1.D6_PWM, LCD1.DB4
  N9: Componente1.D7, LCD1.E
  5V: Componente1.5V, LCD1.VDD, R1.leg2, R2.Pin_1, S1.Pin_3, S1.Pin_4, S2.Pin_3, S2.Pin_4
  GND: Componente1.GND, LCD1.VSS, LCD1.R/W, LCD1.LED-, R1.leg1, R3.Pin_1, R4.Pin_1
  N10: LCD1.V0, R1.wiper
  N11: LCD1.LED+, R2.Pin_0
